# Fritzing sketch one_list_of_LEDs_and_one_push_button (saved by Fritzing 0.9.6b)
breadboards: 1

parts:
  Mod2 = Raspberry Pi 4B
  S1 = Pushbutton [package="[THT]"]
  R1 = Resistor [tolerance=±5% power=0.25 resistance=10k package=THT]
  R2 = Resistor [tolerance=±5% power=0.25 resistance=1k package=THT]
  LED2 = LED - 3mm [color="Red (633nm)" current=0.030 package="3 mm [THT]"]
  R3 = Resistor [tolerance=±5% resistance=1k package="1206 [SMD]"]
  LED3 = LED - 3mm [color="Blue (430nm)" current=0.030 package="3 mm [THT]"]
  R4 = Resistor [tolerance=±5% resistance=1k package="1206 [SMD]"]
  LED4 = LED - 3mm [color="Green (555nm)" current=0.030 package="3 mm [THT]"]
  R5 = Resistor [tolerance=±5% resistance=1k package="1206 [SMD]"]

nets:
  N1: Mod2.3V3, S1.Pin_1, S1.Pin_2
  N2: Mod2.GND, Mod2.GPIO15, R1.Pin_0, LED2.cathode, LED3.cathode, LED4.cathode
  N3: Mod2.GPIO17, R3.Pin_1
  N4: Mod2.GPIO27, R4.Pin_1
  N5: Mod2.GPIO22, R5.Pin_1
  N6: Mod2.GPIO26, R2.Pin_0
  N7: S1.Pin_3, S1.Pin_4, R1.Pin_1, R2.Pin_1
  N8: LED2.anode, R3.Pin_0
  N9: LED3.anode, R4.Pin_0
  N10: LED4.anode, R5.Pin_0
