# Fritzing sketch PIR_sensor (saved by Fritzing 0.9.6b)
breadboards: 1

parts:
  Mod2 = Raspberry Pi 4B
  Composant1 = HC-SR501 Body Sensor Module
  R6 = Resistor [tolerance=±5% power=0.25 resistance=10k package=THT]

nets:
  5V: Mod2.5V, Composant1.VCC
  GND: Mod2.GND, Mod2.GPIO15, Composant1.GND
  N1: Mod2.GPIO4, R6.Pin_0
  N2: Composant1.OUT, R6.Pin_1

custom parts:
  HC-SR501 Body Sensor Module: Pyroelectric Infrared PIR Motion Sensor Detector Module
