# Fritzing sketch push_button_from_Flask (saved by Fritzing 0.9.6b)
breadboards: 1

parts:
  Mod2 = Raspberry Pi 4B
  S1 = Pushbutton [package="[THT]"]
  R1 = Resistor [tolerance=±5% power=0.25 resistance=10k package=THT]
  R2 = Resistor [tolerance=±5% power=0.25 resistance=1k package=THT]

nets:
  N1: Mod2.3V3, S1.Pin_1, S1.Pin_2
  N2: Mod2.GND, Mod2.GPIO15, R1.Pin_0
  N3: Mod2.GPIO26, R2.Pin_0
  N4: S1.Pin_3, S1.Pin_4, R1.Pin_1, R2.Pin_1
