# Fritzing sketch LED (saved by Fritzing 0.9.6b)
breadboards: 1

parts:
  Mod2 = Raspberry Pi 4B
  LED1 = LED - 3mm [color="Red (633nm)" current=0.030 package="3 mm [THT]"]
  R1 = Resistor [tolerance=±5% resistance=1k package="1206 [SMD]"]

nets:
  N1: Mod2.GND, Mod2.GPIO15, LED1.cathode
  N2: Mod2.GPIO17, R1.Pin_1
  N3: LED1.anode, R1.Pin_0
