# Fritzing sketch one_LED_with_one_PIR_sensor (saved by Fritzing 0.9.6b)
breadboards: 1

parts:
  Mod2 = Raspberry Pi 4B
  LED2 = LED - 3mm [color="Red (633nm)" current=0.030 package="3 mm [THT]"]
  R3 = Resistor [tolerance=±5% resistance=1k package="1206 [SMD]"]
  Composant1 = HC-SR501 Body Sensor Module
  R6 = Resistor [tolerance=±5% power=0.25 resistance=10k package=THT]

nets:
  5V: Mod2.5V, Composant1.VCC
  GND: Mod2.GND, Mod2.GPIO15, LED2.cathode, Composant1.GND
  N1: Mod2.GPIO4, R6.Pin_0
  N2: Mod2.GPIO17, R3.Pin_1
  N3: LED2.anode, R3.Pin_0
  N4: Composant1.OUT, R6.Pin_1

custom parts:
  HC-SR501 Body Sensor Module: Pyroelectric Infrared PIR Motion Sensor Detector Module
