# Fritzing sketch one_list_of_LEDs_and_one_PIR_sensor (saved by Fritzing 0.9.6b)
breadboards: 1

parts:
  Mod2 = Raspberry Pi 4B
  LED2 = LED - 3mm [color="Red (633nm)" current=0.030 package="3 mm [THT]"]
  R3 = Resistor [tolerance=±5% resistance=1k package="1206 [SMD]"]
  LED3 = LED - 3mm [color="Blue (430nm)" current=0.030 package="3 mm [THT]"]
  R4 = Resistor [tolerance=±5% resistance=1k package="1206 [SMD]"]
  LED4 = LED - 3mm [color="Green (555nm)" current=0.030 package="3 mm [THT]"]
  R5 = Resistor [tolerance=±5% resistance=1k package="1206 [SMD]"]
  Composant1 = HC-SR501 Body Sensor Module
  R6 = Resistor [tolerance=±5% power=0.25 resistance=10k package=THT]

nets:
  5V: Mod2.5V, Composant1.VCC
  GND: Mod2.GND, Mod2.GPIO15, LED2.cathode, LED3.cathode, LED4.cathode, Composant1.GND
  N1: Mod2.GPIO4, R6.Pin_0
  N2: Mod2.GPIO17, R3.Pin_1
  N3: Mod2.GPIO27, R4.Pin_1
  N4: Mod2.GPIO22, R5.Pin_1
  N5: LED2.anode, R3.Pin_0
  N6: LED3.anode, R4.Pin_0
  N7: LED4.anode, R5.Pin_0
  N8: Composant1.OUT, R6.Pin_1

custom parts:
  HC-SR501 Body Sensor Module: Pyroelectric Infrared PIR Motion Sensor Detector Module
